# Fritzing sketch arduino-schematics (saved by Fritzing 0.9.3b)
breadboards: 1

parts:
  Part1 = Arduino Nano (Rev3.0)
  Q1 = NPN-Transistor [package="TO92 [THT]"]
  R2 = Resistor [tolerance=±5% resistance=1k package=THT]
  R4 = Resistor [tolerance=±5% resistance=1k package=THT]
  R5 = Resistor [tolerance=±5% resistance=1k package=THT]
  U1 = mystery part, 3 pins [chip_label="Soil sensor"]
  U2 = mystery part, 3 pins [chip_label="dht temp&hum"]
  LED1 = LED - 5mm [color="Red (633nm)" package="5 mm [THT]"]

nets:
  N1: Part1.RESET, R5.Pin_1
  N2: Part1.GND, Q1.C, R4.Pin_0, U1.pin1, U1.pin2, U2.pin2
  N3: Part1.D4, U2.pin3
  N4: Part1.D6, LED1.anode
  N5: Part1.D10, R2.Pin_1
  N6: Part1.5V, U2.pin1
  N7: Part1.A0, U1.pin3
  N8: Q1.E, R5.Pin_0
  N9: Q1.B, R2.Pin_0
  N10: R4.Pin_1, LED1.cathode
